// Logisim project ALU.circ as structural Verilog: 8 circuits, main circuit 8bit mult
module _8bit_RCAdder (
  input  in_1,
  input  in_2,
  input  in_3,
  input  in_4,
  input  in_5,
  input  in_6,
  input  in_7,
  input  in_8,
  input  in_9,
  input  in_10,
  input  in_11,
  input  in_12,
  input  in_13,
  input  in_14,
  input  in_15,
  input  in_16,
  input  in_17,
  output out_18,
  output out_19,
  output out_20,
  output out_21,
  output out_22,
  output out_23,
  output out_24,
  output out_25,
  output out_26
);

  wire FA2_cout, FA3_cout, FA4_cout, FA5_cout, FA6_cout, FA7_cout, FA8_cout;

  Full_Adder FA1 (.A(in_9), .B(in_1), .Cin(FA2_cout), .Cout(out_18), .Sum(out_19));
  Full_Adder FA2 (.A(in_10), .B(in_2), .Cin(FA3_cout), .Cout(FA2_cout), .Sum(out_20));
  Full_Adder FA3 (.A(in_11), .B(in_3), .Cin(FA4_cout), .Cout(FA3_cout), .Sum(out_21));
  Full_Adder FA4 (.A(in_12), .B(in_4), .Cin(FA5_cout), .Cout(FA4_cout), .Sum(out_22));
  Full_Adder FA5 (.A(in_13), .B(in_5), .Cin(FA6_cout), .Cout(FA5_cout), .Sum(out_23));
  Full_Adder FA6 (.A(in_14), .B(in_6), .Cin(FA7_cout), .Cout(FA6_cout), .Sum(out_24));
  Full_Adder FA7 (.A(in_15), .B(in_7), .Cin(FA8_cout), .Cout(FA7_cout), .Sum(out_25));
  Full_Adder FA8 (.A(in_16), .B(in_8), .Cin(in_17), .Cout(FA8_cout), .Sum(out_26));
endmodule

module Full_Adder (
  input  A,
  input  B,
  input  Cin,
  output Cout,
  output Sum
);

  wire and_1_out, and_2_out, xor_1_out;

  and and_1 (and_1_out, A, B);
  xor xor_1 (xor_1_out, B, A);
  and and_2 (and_2_out, xor_1_out, Cin);
  or or_1 (Cout, and_1_out, and_2_out);
  xor xor_2 (Sum, xor_1_out, Cin);
endmodule

module _8bit_ALU (
  input  [7:0] A,
  input  [7:0] B,
  input  ADD_SUB,
  input  [2:0] Op_Switch,
  output [15:0] RES,
  output Overflow,
  output out_7
);

  wire [7:0] adder_1_out, bit_extender_1_out, multiplexer_1_out, multiplexer_2_out, n8bit_and_1_out_24,
       n8bit_csadder_1_out_20, n8bit_or_1_out_24, n8bit_xor_1_out_24, not_1_out;
  wire [15:0] bit_extender_2_out, n8bit_mult_1_out_32;

  assign not_1_out = ~B;  // NOT_Gate not_1, 8 bits wide
  Multiplexer #(.width(8), .enable("false")) multiplexer_1 (
    .in0(B), .in1(not_1_out), .out(multiplexer_1_out), .sel(ADD_SUB));
  _8bit_CSAdder u_8bit_csadder_1 (
    .out_18(Overflow), .in_17(ADD_SUB), .A(A[7]), .in_10(A[6]), .in_11(A[5]), .in_12(A[4]), .in_13(A[3]),
    .in_14(A[2]), .in_15(A[1]), .in_16(A[0]), .B(multiplexer_1_out[7]), .in_2(multiplexer_1_out[6]),
    .in_3(multiplexer_1_out[5]), .in_4(multiplexer_1_out[4]), .in_5(multiplexer_1_out[3]),
    .in_6(multiplexer_1_out[2]), .in_7(multiplexer_1_out[1]), .in_8(multiplexer_1_out[0]),
    .out_24(n8bit_csadder_1_out_20[4]), .out_25(n8bit_csadder_1_out_20[3]),
    .out_26(n8bit_csadder_1_out_20[2]), .out_19(n8bit_csadder_1_out_20[1]),
    .out_20(n8bit_csadder_1_out_20[0]), .out_21(n8bit_csadder_1_out_20[7]),
    .out_22(n8bit_csadder_1_out_20[6]), .out_23(n8bit_csadder_1_out_20[5]));
  assign bit_extender_1_out = {{7{1'b0}}, ADD_SUB};  // Bit_Extender bit_extender_1
  _8bit_mult u_8bit_mult_1 (
    .B(A[7]), .in_10(A[6]), .in_11(A[5]), .in_12(A[4]), .in_13(A[3]), .in_14(A[2]), .in_15(A[1]),
    .in_16(A[0]), .A(adder_1_out[7]), .in_2(adder_1_out[6]), .in_3(adder_1_out[5]), .in_4(adder_1_out[4]),
    .in_5(adder_1_out[3]), .in_6(adder_1_out[2]), .in_7(adder_1_out[1]), .in_8(adder_1_out[0]),
    .out_26(n8bit_mult_1_out_32[6]), .out_27(n8bit_mult_1_out_32[5]), .out_28(n8bit_mult_1_out_32[4]),
    .out_29(n8bit_mult_1_out_32[3]), .out_30(n8bit_mult_1_out_32[2]), .out_31(n8bit_mult_1_out_32[1]),
    .out_32(n8bit_mult_1_out_32[0]), .out_25(n8bit_mult_1_out_32[7]), .out_17(n8bit_mult_1_out_32[15]),
    .out_18(n8bit_mult_1_out_32[14]), .out_19(n8bit_mult_1_out_32[13]), .out_20(n8bit_mult_1_out_32[12]),
    .out_21(n8bit_mult_1_out_32[11]), .out_22(n8bit_mult_1_out_32[10]), .out_23(n8bit_mult_1_out_32[9]),
    .out_24(n8bit_mult_1_out_32[8]));
  Adder adder_1 (.a(multiplexer_1_out), .b(bit_extender_1_out), .out(adder_1_out), .cin(1'b0), .cout(out_7));
  _8bit_AND u_8bit_and_1 (
    .out_17(n8bit_and_1_out_24[7]), .out_18(n8bit_and_1_out_24[6]), .out_19(n8bit_and_1_out_24[5]),
    .out_20(n8bit_and_1_out_24[4]), .out_21(n8bit_and_1_out_24[3]), .out_22(n8bit_and_1_out_24[2]),
    .out_23(n8bit_and_1_out_24[1]), .out_24(n8bit_and_1_out_24[0]), .in_1(A[7]), .in_2(A[6]), .in_3(A[5]),
    .in_4(A[4]), .in_5(A[3]), .in_6(A[2]), .in_7(A[1]), .in_8(A[0]), .in_9(multiplexer_1_out[7]),
    .in_10(multiplexer_1_out[6]), .in_11(multiplexer_1_out[5]), .in_12(multiplexer_1_out[4]),
    .in_13(multiplexer_1_out[3]), .in_14(multiplexer_1_out[2]), .in_15(multiplexer_1_out[1]),
    .in_16(multiplexer_1_out[0]));
  _8bit_OR u_8bit_or_1 (
    .out_17(n8bit_or_1_out_24[7]), .out_18(n8bit_or_1_out_24[6]), .out_19(n8bit_or_1_out_24[5]),
    .out_20(n8bit_or_1_out_24[4]), .out_21(n8bit_or_1_out_24[3]), .out_22(n8bit_or_1_out_24[2]),
    .out_23(n8bit_or_1_out_24[1]), .out_24(n8bit_or_1_out_24[0]), .in_1(A[7]), .in_2(A[6]), .in_3(A[5]),
    .in_4(A[4]), .in_5(A[3]), .in_6(A[2]), .in_7(A[1]), .in_8(A[0]), .in_9(multiplexer_1_out[7]),
    .in_10(multiplexer_1_out[6]), .in_11(multiplexer_1_out[5]), .in_12(multiplexer_1_out[4]),
    .in_13(multiplexer_1_out[3]), .in_14(multiplexer_1_out[2]), .in_15(multiplexer_1_out[1]),
    .in_16(multiplexer_1_out[0]));
  _8bit_XOR u_8bit_xor_1 (
    .out_17(n8bit_xor_1_out_24[7]), .out_18(n8bit_xor_1_out_24[6]), .out_19(n8bit_xor_1_out_24[5]),
    .out_20(n8bit_xor_1_out_24[4]), .out_21(n8bit_xor_1_out_24[3]), .out_22(n8bit_xor_1_out_24[2]),
    .out_23(n8bit_xor_1_out_24[1]), .out_24(n8bit_xor_1_out_24[0]), .in_1(A[7]), .in_2(A[6]), .in_3(A[5]),
    .in_4(A[4]), .in_5(A[3]), .in_6(A[2]), .in_7(A[1]), .in_8(A[0]), .in_9(multiplexer_1_out[7]),
    .in_10(multiplexer_1_out[6]), .in_11(multiplexer_1_out[5]), .in_12(multiplexer_1_out[4]),
    .in_13(multiplexer_1_out[3]), .in_14(multiplexer_1_out[2]), .in_15(multiplexer_1_out[1]),
    .in_16(multiplexer_1_out[0]));
  Multiplexer #(.select(2), .width(8), .enable("false")) multiplexer_2 (
    .in0(n8bit_and_1_out_24), .in1(n8bit_or_1_out_24), .in2(n8bit_xor_1_out_24),
    .in3(n8bit_csadder_1_out_20), .out(multiplexer_2_out), .sel(Op_Switch[2:1]));
  assign bit_extender_2_out = {{8{1'b0}}, multiplexer_2_out};  // Bit_Extender bit_extender_2
  Multiplexer #(.width(16), .enable("false")) multiplexer_3 (
    .in0(bit_extender_2_out), .in1(n8bit_mult_1_out_32), .out(RES), .sel(Op_Switch[0]));
endmodule

module _8bit_AND (
  input  in_1,
  input  in_2,
  input  in_3,
  input  in_4,
  input  in_5,
  input  in_6,
  input  in_7,
  input  in_8,
  input  in_9,
  input  in_10,
  input  in_11,
  input  in_12,
  input  in_13,
  input  in_14,
  input  in_15,
  input  in_16,
  output out_17,
  output out_18,
  output out_19,
  output out_20,
  output out_21,
  output out_22,
  output out_23,
  output out_24
);

  and and_1 (out_17, in_1, in_9);
  and and_2 (out_18, in_2, in_10);
  and and_3 (out_19, in_3, in_11);
  and and_4 (out_20, in_4, in_12);
  and and_5 (out_21, in_5, in_13);
  and and_6 (out_22, in_6, in_14);
  and and_7 (out_23, in_7, in_15);
  and and_8 (out_24, in_8, in_16);
endmodule

module _8bit_OR (
  input  in_1,
  input  in_2,
  input  in_3,
  input  in_4,
  input  in_5,
  input  in_6,
  input  in_7,
  input  in_8,
  input  in_9,
  input  in_10,
  input  in_11,
  input  in_12,
  input  in_13,
  input  in_14,
  input  in_15,
  input  in_16,
  output out_17,
  output out_18,
  output out_19,
  output out_20,
  output out_21,
  output out_22,
  output out_23,
  output out_24
);

  or or_1 (out_17, in_1, in_9);
  or or_2 (out_18, in_2, in_10);
  or or_3 (out_19, in_3, in_11);
  or or_4 (out_20, in_4, in_12);
  or or_5 (out_21, in_5, in_13);
  or or_6 (out_22, in_6, in_14);
  or or_7 (out_23, in_7, in_15);
  or or_8 (out_24, in_8, in_16);
endmodule

module _8bit_XOR (
  input  in_1,
  input  in_2,
  input  in_3,
  input  in_4,
  input  in_5,
  input  in_6,
  input  in_7,
  input  in_8,
  input  in_9,
  input  in_10,
  input  in_11,
  input  in_12,
  input  in_13,
  input  in_14,
  input  in_15,
  input  in_16,
  output out_17,
  output out_18,
  output out_19,
  output out_20,
  output out_21,
  output out_22,
  output out_23,
  output out_24
);

  xor xor_1 (out_17, in_1, in_9);
  xor xor_2 (out_18, in_2, in_10);
  xor xor_3 (out_19, in_3, in_11);
  xor xor_4 (out_20, in_4, in_12);
  xor xor_5 (out_21, in_5, in_13);
  xor xor_6 (out_22, in_6, in_14);
  xor xor_7 (out_23, in_7, in_15);
  xor xor_8 (out_24, in_8, in_16);
endmodule

module _8bit_CSAdder (
  input  B,
  input  in_2,
  input  in_3,
  input  in_4,
  input  in_5,
  input  in_6,
  input  in_7,
  input  in_8,
  input  A,
  input  in_10,
  input  in_11,
  input  in_12,
  input  in_13,
  input  in_14,
  input  in_15,
  input  in_16,
  input  in_17,
  output out_18,
  output out_19,
  output out_20,
  output out_21,
  output out_22,
  output out_23,
  output out_24,
  output out_25,
  output out_26
);

  wire FA4_2_cout, FA4_2_sum, FA4_cout, FA4_sum, FA5_2_cout, FA5_2_sum, FA5_3_cout, FA5_3_sum, FA5_4_cout,
       FA5_4_sum, FA5_cout, FA5_sum, FA6_2_cout, FA6_2_sum, FA6_3_cout, FA6_3_sum, FA6_4_cout, FA6_4_sum,
       FA6_5_cout, FA6_5_sum, FA6_6_cout, FA6_6_sum, FA6_cout, FA6_sum, FA7_cout, FA8_cout, multiplexer_5_out;

  Multiplexer #(.enable("false")) multiplexer_1 (.in0(FA4_cout), .in1(FA6_cout), .out(out_18), .sel(multiplexer_5_out));
  Full_Adder FA4 (.A(A), .B(B), .Cin(FA5_cout), .Cout(FA4_cout), .Sum(FA4_sum));
  Full_Adder FA6 (.A(A), .B(B), .Cin(FA5_2_cout), .Cout(FA6_cout), .Sum(FA6_sum));
  Multiplexer #(.enable("false")) multiplexer_2 (.in0(FA4_sum), .in1(FA6_sum), .out(out_21), .sel(multiplexer_5_out));
  Full_Adder FA5 (.A(in_10), .B(in_2), .Cin(FA6_2_cout), .Cout(FA5_cout), .Sum(FA5_sum));
  Full_Adder FA5_2 (.A(in_10), .B(in_2), .Cin(FA6_3_cout), .Cout(FA5_2_cout), .Sum(FA5_2_sum));
  Multiplexer #(.enable("false")) multiplexer_3 (.in0(FA5_sum), .in1(FA5_2_sum), .out(out_22), .sel(multiplexer_5_out));
  Full_Adder FA6_2 (.A(in_11), .B(in_3), .Cin(1'b0), .Cout(FA6_2_cout), .Sum(FA6_2_sum));
  Full_Adder FA6_3 (.A(in_11), .B(in_3), .Cin(1'b1), .Cout(FA6_3_cout), .Sum(FA6_3_sum));
  Multiplexer #(.enable("false")) multiplexer_4 (
    .in0(FA6_2_sum), .in1(FA6_3_sum), .out(out_23), .sel(multiplexer_5_out));
  Multiplexer #(.enable("false")) multiplexer_5 (
    .in0(FA4_2_cout), .in1(FA6_4_cout), .out(multiplexer_5_out), .sel(FA7_cout));
  Full_Adder FA4_2 (.A(in_12), .B(in_4), .Cin(FA5_3_cout), .Cout(FA4_2_cout), .Sum(FA4_2_sum));
  Full_Adder FA6_4 (.A(in_12), .B(in_4), .Cin(FA5_4_cout), .Cout(FA6_4_cout), .Sum(FA6_4_sum));
  Multiplexer #(.enable("false")) multiplexer_6 (.in0(FA4_2_sum), .in1(FA6_4_sum), .out(out_24), .sel(FA7_cout));
  Full_Adder FA5_3 (.A(in_13), .B(in_5), .Cin(FA6_5_cout), .Cout(FA5_3_cout), .Sum(FA5_3_sum));
  Full_Adder FA5_4 (.A(in_13), .B(in_5), .Cin(FA6_6_cout), .Cout(FA5_4_cout), .Sum(FA5_4_sum));
  Multiplexer #(.enable("false")) multiplexer_7 (.in0(FA5_3_sum), .in1(FA5_4_sum), .out(out_25), .sel(FA7_cout));
  Full_Adder FA6_5 (.A(in_14), .B(in_6), .Cin(1'b0), .Cout(FA6_5_cout), .Sum(FA6_5_sum));
  Full_Adder FA6_6 (.A(in_14), .B(in_6), .Cin(1'b1), .Cout(FA6_6_cout), .Sum(FA6_6_sum));
  Multiplexer #(.enable("false")) multiplexer_8 (.in0(FA6_5_sum), .in1(FA6_6_sum), .out(out_26), .sel(FA7_cout));
  Full_Adder FA7 (.A(in_15), .B(in_7), .Cin(FA8_cout), .Cout(FA7_cout), .Sum(out_19));
  Full_Adder FA8 (.A(in_16), .B(in_8), .Cin(in_17), .Cout(FA8_cout), .Sum(out_20));
endmodule

module _8bit_mult (
  input  A,
  input  in_2,
  input  in_3,
  input  in_4,
  input  in_5,
  input  in_6,
  input  in_7,
  input  in_8,
  input  B,
  input  in_10,
  input  in_11,
  input  in_12,
  input  in_13,
  input  in_14,
  input  in_15,
  input  in_16,
  output out_17,
  output out_18,
  output out_19,
  output out_20,
  output out_21,
  output out_22,
  output out_23,
  output out_24,
  output out_25,
  output out_26,
  output out_27,
  output out_28,
  output out_29,
  output out_30,
  output out_31,
  output out_32
);

  wire and_1_out, and_2_out, and_3_out, and_4_out, and_5_out, and_6_out, and_7_out, and_8_out, and_9_out,
       and_10_out, and_11_out, and_12_out, and_13_out, and_14_out, and_15_out, and_16_out, and_17_out,
       and_18_out, and_19_out, and_20_out, and_21_out, and_22_out, and_23_out, and_24_out, and_25_out,
       and_26_out, and_27_out, and_28_out, and_29_out, and_30_out, and_31_out, and_32_out, and_33_out,
       and_34_out, and_35_out, and_36_out, and_37_out, and_38_out, and_39_out, and_40_out, and_41_out,
       and_42_out, and_43_out, and_44_out, and_45_out, and_46_out, and_47_out, and_48_out, and_50_out,
       and_51_out, and_52_out, and_53_out, and_54_out, and_55_out, and_56_out, and_57_out, and_58_out,
       and_59_out, and_60_out, and_61_out, and_62_out, and_63_out, and_64_out, n8bit_csadder_1_out_18,
       n8bit_csadder_1_out_19, n8bit_csadder_1_out_21, n8bit_csadder_1_out_22, n8bit_csadder_1_out_23,
       n8bit_csadder_1_out_24, n8bit_csadder_1_out_25, n8bit_csadder_1_out_26, n8bit_csadder_2_out_18,
       n8bit_csadder_2_out_19, n8bit_csadder_2_out_21, n8bit_csadder_2_out_22, n8bit_csadder_2_out_23,
       n8bit_csadder_2_out_24, n8bit_csadder_2_out_25, n8bit_csadder_2_out_26, n8bit_csadder_3_out_18,
       n8bit_csadder_3_out_19, n8bit_csadder_3_out_21, n8bit_csadder_3_out_22, n8bit_csadder_3_out_23,
       n8bit_csadder_3_out_24, n8bit_csadder_3_out_25, n8bit_csadder_3_out_26, n8bit_csadder_4_out_18,
       n8bit_csadder_4_out_19, n8bit_csadder_4_out_21, n8bit_csadder_4_out_22, n8bit_csadder_4_out_23,
       n8bit_csadder_4_out_24, n8bit_csadder_4_out_25, n8bit_csadder_4_out_26, n8bit_csadder_5_out_18,
       n8bit_csadder_5_out_19, n8bit_csadder_5_out_21, n8bit_csadder_5_out_22, n8bit_csadder_5_out_23,
       n8bit_csadder_5_out_24, n8bit_csadder_5_out_25, n8bit_csadder_5_out_26, n8bit_csadder_6_out_18,
       n8bit_csadder_6_out_19, n8bit_csadder_6_out_21, n8bit_csadder_6_out_22, n8bit_csadder_6_out_23,
       n8bit_csadder_6_out_24, n8bit_csadder_6_out_25, n8bit_csadder_6_out_26;

  and and_1 (and_1_out, in_16, A);
  and and_2 (and_2_out, in_15, A);
  and and_3 (and_3_out, in_14, A);
  and and_4 (and_4_out, in_13, A);
  and and_5 (and_5_out, in_12, A);
  and and_6 (and_6_out, in_11, A);
  and and_7 (and_7_out, in_10, A);
  and and_8 (and_8_out, B, A);
  and and_9 (and_9_out, in_16, in_2);
  _8bit_CSAdder u_8bit_csadder_1 (
    .out_18(n8bit_csadder_1_out_18), .in_17(1'b0), .A(and_1_out), .in_10(and_9_out), .in_11(and_25_out),
    .in_12(and_24_out), .in_13(1'b0), .in_14(and_33_out), .in_15(and_41_out), .in_16(and_50_out),
    .B(and_2_out), .in_2(and_11_out), .in_3(and_10_out), .in_4(and_26_out), .in_5(and_34_out),
    .in_6(and_42_out), .in_7(and_51_out), .in_8(and_52_out), .out_24(n8bit_csadder_1_out_24),
    .out_25(n8bit_csadder_1_out_25), .out_26(n8bit_csadder_1_out_26), .out_19(n8bit_csadder_1_out_19),
    .out_20(out_31), .out_21(n8bit_csadder_1_out_21), .out_22(n8bit_csadder_1_out_22),
    .out_23(n8bit_csadder_1_out_23));
  and and_10 (and_10_out, in_15, in_3);
  and and_11 (and_11_out, in_15, in_2);
  _8bit_CSAdder u_8bit_csadder_2 (
    .out_18(n8bit_csadder_2_out_18), .in_17(1'b0), .A(n8bit_csadder_1_out_18),
    .in_10(n8bit_csadder_1_out_21), .in_11(n8bit_csadder_1_out_22), .in_12(n8bit_csadder_1_out_23),
    .in_13(n8bit_csadder_1_out_24), .in_14(n8bit_csadder_1_out_25), .in_15(n8bit_csadder_1_out_26),
    .in_16(n8bit_csadder_1_out_19), .B(and_3_out), .in_2(and_13_out), .in_3(and_12_out), .in_4(and_27_out),
    .in_5(and_35_out), .in_6(and_43_out), .in_7(and_53_out), .in_8(and_54_out),
    .out_24(n8bit_csadder_2_out_24), .out_25(n8bit_csadder_2_out_25), .out_26(n8bit_csadder_2_out_26),
    .out_19(n8bit_csadder_2_out_19), .out_20(out_30), .out_21(n8bit_csadder_2_out_21),
    .out_22(n8bit_csadder_2_out_22), .out_23(n8bit_csadder_2_out_23));
  and and_12 (and_12_out, in_14, in_3);
  and and_13 (and_13_out, in_14, in_2);
  _8bit_CSAdder u_8bit_csadder_3 (
    .out_18(n8bit_csadder_3_out_18), .in_17(1'b0), .A(n8bit_csadder_2_out_18),
    .in_10(n8bit_csadder_2_out_21), .in_11(n8bit_csadder_2_out_22), .in_12(n8bit_csadder_2_out_23),
    .in_13(n8bit_csadder_2_out_24), .in_14(n8bit_csadder_2_out_25), .in_15(n8bit_csadder_2_out_26),
    .in_16(n8bit_csadder_2_out_19), .B(and_4_out), .in_2(and_14_out), .in_3(and_15_out), .in_4(and_28_out),
    .in_5(and_36_out), .in_6(and_44_out), .in_7(and_55_out), .in_8(and_56_out),
    .out_24(n8bit_csadder_3_out_24), .out_25(n8bit_csadder_3_out_25), .out_26(n8bit_csadder_3_out_26),
    .out_19(n8bit_csadder_3_out_19), .out_20(out_29), .out_21(n8bit_csadder_3_out_21),
    .out_22(n8bit_csadder_3_out_22), .out_23(n8bit_csadder_3_out_23));
  and and_14 (and_14_out, in_13, in_2);
  and and_15 (and_15_out, in_13, in_3);
  _8bit_CSAdder u_8bit_csadder_4 (
    .out_18(n8bit_csadder_4_out_18), .in_17(1'b0), .A(n8bit_csadder_3_out_18),
    .in_10(n8bit_csadder_3_out_21), .in_11(n8bit_csadder_3_out_22), .in_12(n8bit_csadder_3_out_23),
    .in_13(n8bit_csadder_3_out_24), .in_14(n8bit_csadder_3_out_25), .in_15(n8bit_csadder_3_out_26),
    .in_16(n8bit_csadder_3_out_19), .B(and_5_out), .in_2(and_16_out), .in_3(and_17_out), .in_4(and_29_out),
    .in_5(and_37_out), .in_6(and_45_out), .in_7(and_58_out), .in_8(and_57_out),
    .out_24(n8bit_csadder_4_out_24), .out_25(n8bit_csadder_4_out_25), .out_26(n8bit_csadder_4_out_26),
    .out_19(n8bit_csadder_4_out_19), .out_20(out_28), .out_21(n8bit_csadder_4_out_21),
    .out_22(n8bit_csadder_4_out_22), .out_23(n8bit_csadder_4_out_23));
  and and_16 (and_16_out, in_12, in_2);
  and and_17 (and_17_out, in_12, in_3);
  _8bit_CSAdder u_8bit_csadder_5 (
    .out_18(n8bit_csadder_5_out_18), .in_17(1'b0), .A(n8bit_csadder_4_out_18),
    .in_10(n8bit_csadder_4_out_21), .in_11(n8bit_csadder_4_out_22), .in_12(n8bit_csadder_4_out_23),
    .in_13(n8bit_csadder_4_out_24), .in_14(n8bit_csadder_4_out_25), .in_15(n8bit_csadder_4_out_26),
    .in_16(n8bit_csadder_4_out_19), .B(and_6_out), .in_2(and_18_out), .in_3(and_19_out), .in_4(and_30_out),
    .in_5(and_38_out), .in_6(and_46_out), .in_7(and_60_out), .in_8(and_59_out),
    .out_24(n8bit_csadder_5_out_24), .out_25(n8bit_csadder_5_out_25), .out_26(n8bit_csadder_5_out_26),
    .out_19(n8bit_csadder_5_out_19), .out_20(out_27), .out_21(n8bit_csadder_5_out_21),
    .out_22(n8bit_csadder_5_out_22), .out_23(n8bit_csadder_5_out_23));
  and and_18 (and_18_out, in_11, in_2);
  and and_19 (and_19_out, in_11, in_3);
  _8bit_CSAdder u_8bit_csadder_6 (
    .out_18(n8bit_csadder_6_out_18), .in_17(1'b0), .A(n8bit_csadder_5_out_18),
    .in_10(n8bit_csadder_5_out_21), .in_11(n8bit_csadder_5_out_22), .in_12(n8bit_csadder_5_out_23),
    .in_13(n8bit_csadder_5_out_24), .in_14(n8bit_csadder_5_out_25), .in_15(n8bit_csadder_5_out_26),
    .in_16(n8bit_csadder_5_out_19), .B(and_7_out), .in_2(and_20_out), .in_3(and_21_out), .in_4(and_31_out),
    .in_5(and_39_out), .in_6(and_47_out), .in_7(and_61_out), .in_8(and_62_out),
    .out_24(n8bit_csadder_6_out_24), .out_25(n8bit_csadder_6_out_25), .out_26(n8bit_csadder_6_out_26),
    .out_19(n8bit_csadder_6_out_19), .out_20(out_26), .out_21(n8bit_csadder_6_out_21),
    .out_22(n8bit_csadder_6_out_22), .out_23(n8bit_csadder_6_out_23));
  and and_20 (and_20_out, in_10, in_2);
  and and_21 (and_21_out, in_10, in_3);
  _8bit_CSAdder u_8bit_csadder_7 (
    .out_18(out_17), .in_17(1'b0), .A(n8bit_csadder_6_out_18), .in_10(n8bit_csadder_6_out_21),
    .in_11(n8bit_csadder_6_out_22), .in_12(n8bit_csadder_6_out_23), .in_13(n8bit_csadder_6_out_24),
    .in_14(n8bit_csadder_6_out_25), .in_15(n8bit_csadder_6_out_26), .in_16(n8bit_csadder_6_out_19),
    .B(and_8_out), .in_2(and_23_out), .in_3(and_22_out), .in_4(and_32_out), .in_5(and_40_out),
    .in_6(and_48_out), .in_7(and_64_out), .in_8(and_63_out), .out_24(out_21), .out_25(out_22),
    .out_26(out_23), .out_19(out_24), .out_20(out_25), .out_21(out_18), .out_22(out_19), .out_23(out_20));
  and and_22 (and_22_out, B, in_3);
  and and_23 (and_23_out, B, in_2);
  and and_24 (and_24_out, in_16, in_4);
  and and_25 (and_25_out, in_16, in_3);
  and and_26 (and_26_out, in_15, in_4);
  and and_27 (and_27_out, in_14, in_4);
  and and_28 (and_28_out, in_13, in_4);
  and and_29 (and_29_out, in_12, in_4);
  and and_30 (and_30_out, in_11, in_4);
  and and_31 (and_31_out, in_10, in_4);
  and and_32 (and_32_out, B, in_4);
  and and_33 (and_33_out, in_16, in_5);
  and and_34 (and_34_out, in_15, in_5);
  and and_35 (and_35_out, in_14, in_5);
  and and_36 (and_36_out, in_13, in_5);
  and and_37 (and_37_out, in_12, in_5);
  and and_38 (and_38_out, in_11, in_5);
  and and_39 (and_39_out, in_10, in_5);
  and and_40 (and_40_out, B, in_5);
  and and_41 (and_41_out, in_16, in_6);
  and and_42 (and_42_out, in_15, in_6);
  and and_43 (and_43_out, in_14, in_6);
  and and_44 (and_44_out, in_13, in_6);
  and and_45 (and_45_out, in_12, in_6);
  and and_46 (and_46_out, in_11, in_6);
  and and_47 (and_47_out, in_10, in_6);
  and and_48 (and_48_out, B, in_6);
  and and_49 (out_32, in_16, in_8);
  and and_50 (and_50_out, in_16, in_7);
  and and_51 (and_51_out, in_15, in_7);
  and and_52 (and_52_out, in_15, in_8);
  and and_53 (and_53_out, in_14, in_7);
  and and_54 (and_54_out, in_14, in_8);
  and and_55 (and_55_out, in_13, in_7);
  and and_56 (and_56_out, in_13, in_8);
  and and_57 (and_57_out, in_12, in_8);
  and and_58 (and_58_out, in_12, in_7);
  and and_59 (and_59_out, in_11, in_8);
  and and_60 (and_60_out, in_11, in_7);
  and and_61 (and_61_out, in_10, in_7);
  and and_62 (and_62_out, in_10, in_8);
  and and_63 (and_63_out, B, in_8);
  and and_64 (and_64_out, B, in_7);

  // Notes on the sheet:
  //   C_IN
endmodule
